// Digital circuit lab4_lfsr_rng.dig as structural Verilog
// CS303 Lab 4 pre-lab: 16-bit LFSR pseudo-random generator.
// - LFSR taps: bit0, bit1, bit2, bit7
// - BUTTON0 clock advances the generator
// - 3-bit shift register stores shifted-out bits and feeds a 7-seg hex display
// - LOAD_SEED=1 loads the seed constant on next clock edge
//  - Splitter output 15-1 is only for rebuilding the shifted register body (not an extra tap)
// TODO: replace seed 0x9356 with your own last 4 student-ID digits.
module lab4_lfsr_rng (
  input  BUTTON0,
  input  LOAD_SEED,
  output [2:0] RND
);

  wire [2:0] undriven;
  wire [15:0] LFSR_q, multiplexer_1_out, undriven_2;

  Multiplexer #(.Bits(16)) multiplexer_1 (.in_0(undriven_2), .in_1(16'h9356), .out(multiplexer_1_out));  // open: sel
  Register #(.Bits(16)) LFSR (.D(multiplexer_1_out), .Q(LFSR_q));  // open: C, en
  // XOr xor_1 has open pins: In_1=LFSR_q[0], In_2=LFSR_q[1], out=open
  // XOr xor_2 has open pins: In_1=LFSR_q[2], In_2=LFSR_q[7], out=open
  Register #(.Bits(3)) RAND3 (.D(undriven), .en(1'b1));  // open: C, Q
  // XOr xor_3 is placed but not wired
  Seven_Seg_Hex seven_seg_hex_1 ();  // open: d, dp
endmodule
